// Digital circuit plantilla.dig as structural Verilog
module plantilla (
  input  [7:0] N1,
  input  [7:0] N2,
  input  [7:0] N3,
  input  [7:0] N4,
  input  [7:0] N5,
  input  [4:0] N6,
  input  [4:0] N7,
  input  [4:0] N8,
  input  [4:0] N9,
  input  [4:0] N10,
  input  plus,
  output out_12
);

  wire [4:0] neg_1_out, neg_2_out, neg_3_out, neg_4_out, neg_5_out, neg_6_out, neg_7_out, neg_8_out,
       neg_9_out, neg_10_out;
  wire [7:0] neg_11_out, neg_12_out, neg_13_out, neg_14_out, neg_15_out, neg_16_out, neg_17_out, neg_18_out,
       neg_19_out, neg_20_out;

  Add #(.Bits(5)) add_1 (.c_i(1'b0));  // open: a, b, s, c_o
  Neg #(.Bits(5)) neg_1 (.in(N1[4:0]), .out(neg_1_out));
  Neg #(.Bits(5)) neg_2 (.in(N2[4:0]), .out(neg_2_out));
  Neg #(.Bits(5)) neg_3 (.in(N3[4:0]), .out(neg_3_out));
  Neg #(.Bits(5)) neg_4 (.in(N4[4:0]), .out(neg_4_out));
  Neg #(.Bits(5)) neg_5 (.in(N5[4:0]), .out(neg_5_out));
  Neg #(.Bits(5)) neg_6 (.in(N6), .out(neg_6_out));
  Neg #(.Bits(5)) neg_7 (.in(N7), .out(neg_7_out));
  Neg #(.Bits(5)) neg_8 (.in(N8), .out(neg_8_out));
  Neg #(.Bits(5)) neg_9 (.in(N9), .out(neg_9_out));
  Neg #(.Bits(5)) neg_10 (.in(N10), .out(neg_10_out));
  Neg #(.Bits(8)) neg_11 (.in({3'b000, neg_1_out}), .out(neg_11_out));
  Neg #(.Bits(8)) neg_12 (.in({3'b000, neg_2_out}), .out(neg_12_out));
  Neg #(.Bits(8)) neg_13 (.in({3'b000, neg_3_out}), .out(neg_13_out));
  Neg #(.Bits(8)) neg_14 (.in({3'b000, neg_4_out}), .out(neg_14_out));
  Neg #(.Bits(8)) neg_15 (.in({3'b000, neg_5_out}), .out(neg_15_out));
  Neg #(.Bits(8)) neg_16 (.in({3'b000, neg_6_out}), .out(neg_16_out));
  Neg #(.Bits(8)) neg_17 (.in({3'b000, neg_7_out}), .out(neg_17_out));
  Neg #(.Bits(8)) neg_18 (.in({3'b000, neg_8_out}), .out(neg_18_out));
  Neg #(.Bits(8)) neg_19 (.in({3'b000, neg_9_out}), .out(neg_19_out));
  Neg #(.Bits(8)) neg_20 (.in({3'b000, neg_10_out}), .out(neg_20_out));
  Multiplexer #(.Bits(8)) multiplexer_1 (.sel(N1[4]), .in_0({3'b000, N1[4:0]}), .in_1(neg_11_out), .out(N1));
  Multiplexer #(.Bits(8)) multiplexer_2 (.sel(N2[4]), .in_0({3'b000, N2[4:0]}), .in_1(neg_12_out), .out(N2));
  Multiplexer #(.Bits(8)) multiplexer_3 (.sel(N3[4]), .in_0({3'b000, N3[4:0]}), .in_1(neg_13_out), .out(N3));
  Multiplexer #(.Bits(8)) multiplexer_4 (.sel(N4[4]), .in_0({3'b000, N4[4:0]}), .in_1(neg_14_out), .out(N4));
  Multiplexer #(.Bits(8)) multiplexer_5 (.sel(N5[4]), .in_0({3'b000, N5[4:0]}), .in_1(neg_15_out), .out(N5));
  Multiplexer #(.Bits(8)) multiplexer_6 (.sel(N6[4]), .in_0({3'b000, N6}), .in_1(neg_16_out));  // open: out
  Multiplexer #(.Bits(8)) multiplexer_7 (.sel(N7[4]), .in_0({3'b000, N7}), .in_1(neg_17_out));  // open: out
  Multiplexer #(.Bits(8)) multiplexer_8 (.sel(N8[4]), .in_0({3'b000, N8}), .in_1(neg_18_out));  // open: out
  Multiplexer #(.Bits(8)) multiplexer_9 (.sel(N9[4]), .in_0({3'b000, N9}), .in_1(neg_19_out));  // open: out
  Multiplexer #(.Bits(8)) multiplexer_10 (.sel(N10[4]), .in_0({3'b000, N10}), .in_1(neg_20_out));  // open: out
  // Pins of 5 and 8 bits meet at N1
  // Pins of 5 and 8 bits meet at N2
  // Pins of 5 and 8 bits meet at N3
  // Pins of 5 and 8 bits meet at N4
  // Pins of 5 and 8 bits meet at N5
endmodule
